// Digital circuit Full_Assembly.dig as structural Verilog
module Full_Assembly (
  input  EN_PC,
  input  LOAD_PC,
  input  EO_PC,
  input  CLR_PC,
  input  EO_A,
  input  CLR_A,
  input  LOAD_A,
  input  EO_B,
  input  CLR_B,
  input  LOAD_B,
  input  SU_ALU,
  input  EO_ALU,
  input  EN_MAR,
  input  SEL,
  input  CLR_MAR,
  input  SEL_2,
  input  CLR_MDR,
  input  LOAD_MAR,
  input  in_22,
  input  EO_IR,
  input  CLK,
  input  CLR_IR,
  input  LOAD_IR,
  input  EN_PC_2,
  input  LOAD_PC_2,
  input  EO_PC_2,
  output Z,
  output CAR,
  output NEG
);

  wire _3_STATE_6_pin1, _74163_1_pin11, _74163_1_pin12, _74163_1_pin13, _74163_1_pin14, _74163_2_pin11,
       _74163_2_pin12, _74163_2_pin13, _74163_2_pin14, _74283_1_pin1, _74283_1_pin4, _74283_1_pin13,
       AND_2_pin3, AND_2_pin6, D_3_OUT_2_pin3, D_3_OUT_2_pin4, D_3_OUT_2_pin5, D_3_OUT_2_pin6,
       D_3_OUT_3_pin3, D_3_OUT_3_pin4, D_3_OUT_3_pin5, D_3_OUT_3_pin6, D_3_OUT_4_pin3, D_3_OUT_4_pin4,
       D_3_OUT_4_pin5, D_3_OUT_4_pin6, D_3_OUT_5_pin3, D_3_OUT_5_pin4, D_3_OUT_5_pin5, D_3_OUT_5_pin6,
       D_3_OUT_pin3, D_3_OUT_pin4, D_3_OUT_pin5, D_3_OUT_pin6, D_3_OUT_pin11, D_3_OUT_pin12, D_3_OUT_pin13,
       D_3_OUT_pin14, MUX_2_pin3, MUX_2_pin6, MUX_2_pin10, MUX_2_pin13, MUX_pin3, MUX_pin6, MUX_pin10,
       MUX_pin13, NOT_2_pin2, NOT_2_pin4, NOT_2_pin6, NOT_2_pin8, NOT_pin2, NOT_pin4, NOT_pin10, NOT_pin12,
       SRAM_pin1, SRAM_pin3, SRAM_pin4, SRAM_pin5, SRAM_pin6, SRAM_pin7, SRAM_pin9, SRAM_pin10, SRAM_pin11,
       SRAM_pin12, SRAM_pin13, SRAM_pin14, SRAM_pin15, W_RAM_out, XOR_pin3, XOR_pin6, XOR_pin8, XOR_pin11;

  Button #(.activeLow("true")) W_RAM (.out(W_RAM_out));
  _74173 D_3_OUT (
    .pin1(1'b0), .pin2(1'b0), .pin3(D_3_OUT_pin3), .pin4(D_3_OUT_pin4), .pin5(D_3_OUT_pin5),
    .pin6(D_3_OUT_pin6), .pin7(in_22), .pin8(1'b0), .pin9(LOAD_MAR), .pin10(LOAD_MAR), .pin11(D_3_OUT_pin11),
    .pin12(D_3_OUT_pin12), .pin13(D_3_OUT_pin13), .pin14(D_3_OUT_pin14), .pin15(CLR_MAR), .pin16(1'b1));
  _74189 SRAM (
    .pin1(SRAM_pin1), .pin2(1'b0), .pin3(SRAM_pin3), .pin4(SRAM_pin4), .pin5(SRAM_pin5), .pin6(SRAM_pin6),
    .pin7(SRAM_pin7), .pin8(1'b0), .pin9(SRAM_pin9), .pin10(SRAM_pin10), .pin11(SRAM_pin11),
    .pin12(SRAM_pin12), .pin13(SRAM_pin13), .pin14(SRAM_pin14), .pin15(SRAM_pin15), .pin16(1'b1));
  _74173 D_3_OUT_2 (
    .pin1(1'b0), .pin2(1'b0), .pin3(D_3_OUT_2_pin3), .pin4(D_3_OUT_2_pin4), .pin5(D_3_OUT_2_pin5),
    .pin6(D_3_OUT_2_pin6), .pin7(in_22), .pin8(1'b0), .pin9(LOAD_MAR), .pin10(LOAD_MAR),
    .pin11(D_3_OUT_pin11), .pin12(D_3_OUT_pin12), .pin13(D_3_OUT_pin13), .pin14(D_3_OUT_pin14),
    .pin15(CLR_MDR), .pin16(1'b1));
  _74173 D_3_OUT_3 (
    .pin1(1'b0), .pin2(1'b0), .pin3(D_3_OUT_3_pin3), .pin4(D_3_OUT_3_pin4), .pin5(D_3_OUT_3_pin5),
    .pin6(D_3_OUT_3_pin6), .pin7(CLK), .pin8(1'b0), .pin9(LOAD_IR), .pin10(LOAD_IR), .pin11(D_3_OUT_pin11),
    .pin12(D_3_OUT_pin12), .pin13(D_3_OUT_pin13), .pin14(D_3_OUT_pin14), .pin15(CLR_IR), .pin16(1'b1));
  _74157 MUX (
    .pin1(SEL), .pin2(D_3_OUT_pin3), .pin3(MUX_pin3), .pin4(SRAM_pin1), .pin5(D_3_OUT_pin4), .pin6(MUX_pin6),
    .pin7(SRAM_pin15), .pin8(1'b0), .pin9(SRAM_pin14), .pin10(MUX_pin10), .pin11(D_3_OUT_pin5),
    .pin12(SRAM_pin13), .pin13(MUX_pin13), .pin14(D_3_OUT_pin6), .pin15(1'b0), .pin16(1'b1));
  _7404 NOT (
    .pin1(SRAM_pin5), .pin2(NOT_pin2), .pin3(SRAM_pin7), .pin4(NOT_pin4), .pin5(1'b0), .pin7(1'b0),
    .pin9(1'b0), .pin10(NOT_pin10), .pin11(SRAM_pin9), .pin12(NOT_pin12), .pin13(SRAM_pin11), .pin14(1'b1));  // open: pin6, pin8
  _74157 MUX_2 (
    .pin1(SEL_2), .pin2(D_3_OUT_2_pin3), .pin3(MUX_2_pin3), .pin4(SRAM_pin4), .pin5(D_3_OUT_2_pin4),
    .pin6(MUX_2_pin6), .pin7(SRAM_pin6), .pin8(1'b0), .pin9(SRAM_pin10), .pin10(MUX_2_pin10),
    .pin11(D_3_OUT_2_pin5), .pin12(SRAM_pin12), .pin13(MUX_2_pin13), .pin14(D_3_OUT_2_pin6), .pin15(1'b0),
    .pin16(1'b1));
  _74126 _3_STATE (
    .pin1(EN_MAR), .pin2(NOT_pin2), .pin3(D_3_OUT_pin14), .pin4(EN_MAR), .pin5(NOT_pin4),
    .pin6(D_3_OUT_pin13), .pin7(1'b0), .pin8(D_3_OUT_pin12), .pin9(NOT_pin10), .pin10(EN_MAR),
    .pin11(D_3_OUT_pin11), .pin12(NOT_pin12), .pin13(EN_MAR), .pin14(1'b1));
  _74126 _3_STATE_2 (
    .pin1(EO_IR), .pin2(D_3_OUT_3_pin3), .pin3(D_3_OUT_pin14), .pin4(EO_IR), .pin5(D_3_OUT_3_pin4),
    .pin6(D_3_OUT_pin13), .pin7(1'b0), .pin8(D_3_OUT_pin12), .pin9(D_3_OUT_3_pin5), .pin10(EO_IR),
    .pin11(D_3_OUT_pin11), .pin12(D_3_OUT_3_pin6), .pin13(EO_IR), .pin14(1'b1));
  _7408 AND (
    .pin1(W_RAM_out), .pin2(in_22), .pin3(SRAM_pin3), .pin4(1'b0), .pin5(1'b0), .pin7(1'b0), .pin9(1'b1),
    .pin10(1'b1), .pin12(1'b1), .pin13(1'b1), .pin14(1'b1));  // open: pin6, pin8, pin11
  DipSwitch dipswitch_1 (.out(MUX_pin13));
  DipSwitch dipswitch_2 (.out(MUX_pin10));
  DipSwitch dipswitch_3 (.out(MUX_pin6));
  DipSwitch dipswitch_4 (.out(MUX_pin3));
  DipSwitch dipswitch_5 (.out(MUX_2_pin13));
  DipSwitch dipswitch_6 (.out(MUX_2_pin10));
  DipSwitch dipswitch_7 (.out(MUX_2_pin6));
  DipSwitch dipswitch_8 (.out(MUX_2_pin3));
  _7486 XOR (
    .pin1(SU_ALU), .pin2(D_3_OUT_pin14), .pin3(XOR_pin3), .pin4(SU_ALU), .pin5(D_3_OUT_pin13),
    .pin6(XOR_pin6), .pin7(1'b0), .pin8(XOR_pin8), .pin9(SU_ALU), .pin10(D_3_OUT_pin12), .pin11(XOR_pin11),
    .pin12(SU_ALU), .pin13(D_3_OUT_pin11), .pin14(1'b1));
  _74163 _74163_1 (
    .pin1(CLR_PC), .pin2(in_22), .pin3(D_3_OUT_pin14), .pin4(D_3_OUT_pin13), .pin5(D_3_OUT_pin12),
    .pin6(D_3_OUT_pin11), .pin7(EN_PC), .pin8(1'b0), .pin9(LOAD_PC), .pin10(EN_PC), .pin11(_74163_1_pin11),
    .pin12(_74163_1_pin12), .pin13(_74163_1_pin13), .pin14(_74163_1_pin14), .pin16(1'b1));  // open: pin15
  _74173 D_3_OUT_4 (
    .pin1(1'b0), .pin2(1'b0), .pin3(D_3_OUT_4_pin3), .pin4(D_3_OUT_4_pin4), .pin5(D_3_OUT_4_pin5),
    .pin6(D_3_OUT_4_pin6), .pin7(in_22), .pin8(1'b0), .pin9(LOAD_A), .pin10(LOAD_A), .pin11(D_3_OUT_pin11),
    .pin12(D_3_OUT_pin12), .pin13(D_3_OUT_pin13), .pin14(D_3_OUT_pin14), .pin15(CLR_A), .pin16(1'b1));
  _74163 _74163_2 (
    .pin2(1'b0), .pin3(D_3_OUT_pin14), .pin4(D_3_OUT_pin13), .pin5(D_3_OUT_pin12), .pin6(D_3_OUT_pin11),
    .pin7(EN_PC_2), .pin8(1'b0), .pin9(LOAD_PC_2), .pin10(EN_PC_2), .pin11(_74163_2_pin11),
    .pin12(_74163_2_pin12), .pin13(_74163_2_pin13), .pin14(_74163_2_pin14), .pin16(1'b1));  // open: pin1, pin15
  _74283 _74283_1 (
    .pin1(_74283_1_pin1), .pin2(XOR_pin6), .pin3(D_3_OUT_pin13), .pin4(_74283_1_pin4), .pin5(D_3_OUT_pin14),
    .pin6(XOR_pin3), .pin7(SU_ALU), .pin8(1'b0), .pin9(CAR), .pin10(NEG), .pin11(XOR_pin11),
    .pin12(D_3_OUT_pin11), .pin13(_74283_1_pin13), .pin14(D_3_OUT_pin12), .pin15(XOR_pin8), .pin16(1'b1));
  _74126 _3_STATE_3 (
    .pin1(EO_PC), .pin2(_74163_1_pin14), .pin3(D_3_OUT_pin14), .pin4(EO_PC), .pin5(_74163_1_pin13),
    .pin6(D_3_OUT_pin13), .pin7(1'b0), .pin8(D_3_OUT_pin12), .pin9(_74163_1_pin12), .pin10(EO_PC),
    .pin11(D_3_OUT_pin11), .pin12(_74163_1_pin11), .pin13(EO_PC), .pin14(1'b1));
  _74126 _3_STATE_4 (
    .pin1(EO_PC_2), .pin2(_74163_2_pin14), .pin3(D_3_OUT_pin14), .pin4(EO_PC_2), .pin5(_74163_2_pin13),
    .pin6(D_3_OUT_pin13), .pin7(1'b0), .pin8(D_3_OUT_pin12), .pin9(_74163_2_pin12), .pin10(EO_PC_2),
    .pin11(D_3_OUT_pin11), .pin12(_74163_2_pin11), .pin13(EO_PC_2), .pin14(1'b1));
  _74126 _3_STATE_5 (
    .pin1(EO_A), .pin2(D_3_OUT_4_pin3), .pin3(D_3_OUT_pin14), .pin4(EO_A), .pin5(D_3_OUT_4_pin4),
    .pin6(D_3_OUT_pin13), .pin7(1'b0), .pin8(D_3_OUT_pin12), .pin9(D_3_OUT_4_pin5), .pin10(EO_A),
    .pin11(D_3_OUT_pin11), .pin12(D_3_OUT_4_pin6), .pin13(EO_A), .pin14(1'b1));
  _74126 _3_STATE_6 (
    .pin1(_3_STATE_6_pin1), .pin2(_74283_1_pin4), .pin3(D_3_OUT_pin14), .pin4(_3_STATE_6_pin1),
    .pin5(_74283_1_pin1), .pin6(D_3_OUT_pin13), .pin7(1'b0), .pin8(D_3_OUT_pin12), .pin9(_74283_1_pin13),
    .pin10(_3_STATE_6_pin1), .pin11(D_3_OUT_pin11), .pin12(NEG), .pin13(_3_STATE_6_pin1), .pin14(1'b1));
  _7404 NOT_2 (
    .pin1(_74283_1_pin4), .pin2(NOT_2_pin2), .pin3(_74283_1_pin1), .pin4(NOT_2_pin4), .pin5(_74283_1_pin13),
    .pin6(NOT_2_pin6), .pin7(1'b0), .pin8(NOT_2_pin8), .pin9(NEG), .pin11(1'b1), .pin13(1'b1), .pin14(1'b1));  // open: pin10, pin12
  _74173 D_3_OUT_5 (
    .pin1(1'b0), .pin2(1'b0), .pin3(D_3_OUT_5_pin3), .pin4(D_3_OUT_5_pin4), .pin5(D_3_OUT_5_pin5),
    .pin6(D_3_OUT_5_pin6), .pin7(in_22), .pin8(1'b0), .pin9(LOAD_B), .pin10(LOAD_B), .pin11(D_3_OUT_pin11),
    .pin12(D_3_OUT_pin12), .pin13(D_3_OUT_pin13), .pin14(D_3_OUT_pin14), .pin15(CLR_B), .pin16(1'b1));
  _7408 AND_2 (
    .pin1(NOT_2_pin2), .pin2(NOT_2_pin4), .pin3(AND_2_pin3), .pin4(AND_2_pin3), .pin5(NOT_2_pin6),
    .pin6(AND_2_pin6), .pin7(1'b0), .pin8(Z), .pin9(AND_2_pin6), .pin10(NOT_2_pin8), .pin11(_3_STATE_6_pin1),
    .pin12(in_22), .pin13(EO_ALU), .pin14(1'b1));
  _74126 _3_STATE_7 (
    .pin1(EO_B), .pin2(D_3_OUT_5_pin3), .pin3(D_3_OUT_pin14), .pin4(EO_B), .pin5(D_3_OUT_5_pin4),
    .pin6(D_3_OUT_pin13), .pin7(1'b0), .pin8(D_3_OUT_pin12), .pin9(D_3_OUT_5_pin5), .pin10(EO_B),
    .pin11(D_3_OUT_pin11), .pin12(D_3_OUT_5_pin6), .pin13(EO_B), .pin14(1'b1));

  // Notes on the sheet:
  //   MAR
  //   RAM
  //   MDR
  //   IR
  //   4
  //   3
  //   2
  //   1
  //   CLK
  //   5V
  //   GND
  //   PC
  //   A and B Reg
  //   ALU
  //   OUT Reg
endmodule
